# Fritzing sketch sketch (saved by Fritzing 0.9.5d)

parts:
  Mod1 = Raspberry Pi Pico
  microSD1 = MicroSD Card Module
  A1 = Waveshare 1.54in epaper display
  DFRobot_DFPlayer_Mini1 = DFRobot DFPlayer Mini [part_number=DFR0299]
  SP1 = SPEAKER [package=pcb_mount_speaker]

nets:
  N1: Mod1.pin_6, DFRobot_DFPlayer_Mini1.TX
  N2: Mod1.pin_7, DFRobot_DFPlayer_Mini1.RX
  N3: Mod1.pin_11, A1.Pin_3
  N4: Mod1.pin_12, A1.Pin_4
  N5: Mod1.pin_16, A1.Pin_2
  N6: Mod1.pin_17, A1.Pin_1
  N7: Mod1.pin_21, microSD1.MISO
  N8: Mod1.pin_22, microSD1.CS
  N9: Mod1.pin_24, microSD1.SCK, A1.Pin_5
  N10: Mod1.pin_25, microSD1.MOSI, A1.Pin_6
  N11: Mod1.pin_33, Mod1.pin_38, Mod1.pin_42, microSD1.GND, A1.Pin_7, DFRobot_DFPlayer_Mini1.GND-1
  VCC: Mod1.pin_36, microSD1.VCC, A1.Pin_8, DFRobot_DFPlayer_Mini1.VCC
  N12: DFRobot_DFPlayer_Mini1.SPK_1, SP1.-
  N13: DFRobot_DFPlayer_Mini1.SPK_2, SP1.+

custom parts:
  Raspberry Pi Pico: Raspberry Pi Pico. Based around the RP2040 microcontroller the Pico is a low cost microcontroller device bringing Raspberry Pi quality, cost, and easy of use to the microcontroller space. Jan 2021, Split part in to two versions: tht (this one) and SMD. This one will drill holes for a .1 in header in pcb to allow plugging in the module as well as providing pads to solder the module to the top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
  Waveshare 1.54in epaper display: This is an E-Ink display module, 1.54inch, 200x200 resolution, with embedded controller, communicating via SPI interface.
